# Fritzing sketch wiring (saved by Fritzing 0.9.6b)

parts:
  PIC1 = PIC18F4550 [package="DIP (Dual Inline) [THT]"]
  LCD1 = LCD screen
  R1 = Rotary Potentiometer (Large) [maximum_resistance=100kΩ package=THT]

nets:
  N1: PIC1.RE0/AN5/CK1SPP, LCD1.E
  N2: PIC1.RE1/AN6/CK2SPP, LCD1.R/W
  N3: PIC1.RE2/AN7/OESPP, LCD1.RS
  N4: PIC1.Vdd, LCD1.V0, R1.leg2
  VSS: PIC1.Vss, LCD1.VSS, R1.leg1
  N5: PIC1.RD0/SPP0, LCD1.DB0
  N6: PIC1.RD1/SPP1, LCD1.DB1
  N7: PIC1.RD2/SPP2, LCD1.DB2
  N8: PIC1.RD3/SPP3, LCD1.DB3
  N9: PIC1.RD4/PSP4, LCD1.DB4
  N10: PIC1.RD5/SPP5/P1B, LCD1.DB5
  N11: PIC1.RD6/SPP6/P1C, LCD1.DB6
  N12: PIC1.RD7/SPP7/P1D, LCD1.DB7
  N13: LCD1.VDD, R1.wiper
